// Logisim project memoria.circ as structural Verilog: 2 circuits, main circuit Mem Instr
module Mem_Instr (
  input  [31:0] PC_Adress,
  output [31:0] out_2
);

  ROM #(.addrWidth(24), .dataWidth(32)) rom_1 (.addr(PC_Adress[25:2]), .data(out_2));  // open: sel

  // Notes on the sheet:
  //   contents of rom_1 (hex, n*v repeats v):
  //   2 123412 1234 13*0 234 1324 31243 13*0 2314123 1324 1324 dafad 12*0 cda
endmodule

// MemWrite
module Mem_Dados (
  input  [31:0] A,
  input  MemWrite,
  input  MemRead,
  input  [31:0] B,
  output [31:0] out_5
);

  wire clock_1_out;

  Clock clock_1 (.out(clock_1_out));
  RAM #(.addrWidth(24), .dataWidth(32), .bus("separate")) ram_1 (
    .addr(A[25:2]), .din(B), .data(out_5), .str(MemWrite), .clk(clock_1_out), .ld(MemRead));  // open: sel, clr
endmodule
