// Logisim project computador.circ as structural Verilog: 4 circuits, main circuit main
module main (
  input  [10:0] Entrada,
  input  Leitura_Escrita,
  output [7:0] out_3
);

  wire and_1_out, and_2_out, and_3_out, and_4_out, and_5_out, and_6_out, and_7_out, and_8_out, and_9_out,
       and_10_out, and_11_out, and_12_out, and_13_out, and_14_out, and_15_out, and_16_out, and_17_out,
       and_18_out, and_19_out, and_20_out, and_21_out, and_22_out, and_23_out, and_24_out, and_25_out,
       and_26_out, and_27_out, and_28_out, and_29_out, and_30_out, and_31_out, and_32_out, and_33_out,
       and_34_out, and_35_out, and_36_out, and_37_out, and_38_out, and_39_out, and_40_out, and_41_out,
       and_42_out, and_43_out, and_44_out, and_45_out, and_46_out, and_47_out, and_48_out, and_49_out,
       and_50_out, and_51_out, and_52_out, and_53_out, and_54_out, and_55_out, and_56_out, and_57_out,
       and_58_out, and_59_out, and_60_out, and_61_out, and_62_out, and_63_out, and_64_out, and_65_out,
       and_66_out, and_67_out, and_68_out, and_69_out, and_70_out, and_71_out, and_72_out, and_73_out,
       and_74_out, and_75_out, and_76_out, and_77_out, and_78_out, and_79_out, and_80_out, and_81_out,
       and_82_out, and_83_out, and_84_out, and_85_out, and_86_out, and_87_out, and_88_out, and_89_out,
       and_90_out, and_91_out, and_92_out, and_93_out, and_94_out, and_95_out, and_96_out, and_97_out,
       and_98_out, and_99_out, and_100_out, and_101_out, and_102_out, and_103_out, and_104_out, clock_1_out,
       d_ff_1_q, d_ff_2_q, d_ff_3_q, d_ff_4_q, d_ff_5_q, d_ff_6_q, d_ff_7_q, d_ff_8_q, d_ff_9_q, d_ff_10_q,
       d_ff_11_q, d_ff_12_q, d_ff_13_q, d_ff_14_q, d_ff_15_q, d_ff_16_q, d_ff_17_q, d_ff_18_q, d_ff_19_q,
       d_ff_20_q, d_ff_21_q, d_ff_22_q, d_ff_23_q, d_ff_24_q, d_ff_25_q, d_ff_26_q, d_ff_27_q, d_ff_28_q,
       d_ff_29_q, d_ff_30_q, d_ff_31_q, d_ff_32_q, d_ff_33_q, d_ff_34_q, d_ff_35_q, d_ff_36_q, d_ff_37_q,
       d_ff_38_q, d_ff_39_q, d_ff_40_q, d_ff_41_q, d_ff_42_q, d_ff_43_q, d_ff_44_q, d_ff_45_q, d_ff_46_q,
       d_ff_47_q, d_ff_48_q, d_ff_49_q, d_ff_50_q, d_ff_51_q, d_ff_52_q, d_ff_53_q, d_ff_54_q, d_ff_55_q,
       d_ff_56_q, d_ff_57_q, d_ff_58_q, d_ff_59_q, d_ff_60_q, d_ff_61_q, d_ff_62_q, d_ff_63_q, d_ff_64_q,
       d_ff_65_q, d_ff_66_q, d_ff_67_q, d_ff_68_q, d_ff_69_q, d_ff_70_q, d_ff_71_q, d_ff_72_q, d_ff_73_q,
       d_ff_74_q, d_ff_75_q, d_ff_76_q, d_ff_77_q, d_ff_78_q, d_ff_79_q, d_ff_80_q, d_ff_81_q, d_ff_82_q,
       d_ff_83_q, d_ff_84_q, d_ff_85_q, d_ff_86_q, d_ff_87_q, d_ff_88_q;
  wire [2:0] t_ff_1_q;
  wire [7:0] ula_1_out_4;
  wire [10:0] or_11_out;

  Clock clock_1 (.out(clock_1_out));
  T_Flip_Flop #(.trigger("falling")) t_ff_1 (
    .clk(clock_1_out), .T(1'b1), .Q(t_ff_1_q[0]));  // open: Qn, preset, reset, en
  T_Flip_Flop #(.trigger("falling")) t_ff_2 (
    .clk(t_ff_1_q[0]), .T(1'b1), .Q(t_ff_1_q[1]));  // open: Qn, preset, reset, en
  T_Flip_Flop #(.trigger("falling")) t_ff_3 (
    .clk(t_ff_1_q[1]), .T(1'b1), .Q(t_ff_1_q[2]));  // open: Qn, preset, reset, en
  and and_1 (and_1_out, ~t_ff_1_q[2], ~t_ff_1_q[1], ~t_ff_1_q[0]);  // AND_Gate
  and and_2 (and_2_out, and_1_out, Leitura_Escrita);
  and and_3 (and_3_out, ~t_ff_1_q[2], ~t_ff_1_q[1], t_ff_1_q[0]);  // AND_Gate
  and and_4 (and_4_out, and_3_out, Leitura_Escrita);
  and and_5 (and_5_out, ~t_ff_1_q[2], t_ff_1_q[1], ~t_ff_1_q[0]);  // AND_Gate
  and and_6 (and_6_out, and_5_out, Leitura_Escrita);
  and and_7 (and_7_out, ~t_ff_1_q[2], t_ff_1_q[1], t_ff_1_q[0]);  // AND_Gate
  and and_8 (and_8_out, and_7_out, Leitura_Escrita);
  and and_9 (and_9_out, t_ff_1_q[2], ~t_ff_1_q[1], ~t_ff_1_q[0]);  // AND_Gate
  and and_10 (and_10_out, and_9_out, Leitura_Escrita);
  and and_11 (and_11_out, t_ff_1_q[2], ~t_ff_1_q[1], t_ff_1_q[0]);  // AND_Gate
  and and_12 (and_12_out, and_11_out, Leitura_Escrita);
  and and_13 (and_13_out, t_ff_1_q[2], t_ff_1_q[1], ~t_ff_1_q[0]);  // AND_Gate
  and and_14 (and_14_out, and_13_out, Leitura_Escrita);
  and and_15 (and_15_out, t_ff_1_q[2], t_ff_1_q[1], t_ff_1_q[0]);
  and and_16 (and_16_out, and_15_out, Leitura_Escrita);
  D_Flip_Flop #(.trigger("falling")) d_ff_1 (
    .clk(and_2_out), .D(Entrada[10]), .Q(d_ff_1_q));  // open: Qn, preset, en, reset
  D_Flip_Flop #(.trigger("falling")) d_ff_2 (
    .clk(and_4_out), .D(Entrada[10]), .Q(d_ff_2_q));  // open: Qn, preset, en, reset
  D_Flip_Flop #(.trigger("falling")) d_ff_3 (
    .clk(and_6_out), .D(Entrada[10]), .Q(d_ff_3_q));  // open: Qn, preset, en, reset
  D_Flip_Flop #(.trigger("falling")) d_ff_4 (
    .clk(and_8_out), .D(Entrada[10]), .Q(d_ff_4_q));  // open: Qn, preset, en, reset
  D_Flip_Flop #(.trigger("falling")) d_ff_5 (
    .clk(and_10_out), .D(Entrada[10]), .Q(d_ff_5_q));  // open: Qn, preset, en, reset
  D_Flip_Flop #(.trigger("falling")) d_ff_6 (
    .clk(and_12_out), .D(Entrada[10]), .Q(d_ff_6_q));  // open: Qn, preset, en, reset
  D_Flip_Flop #(.trigger("falling")) d_ff_7 (
    .clk(and_14_out), .D(Entrada[10]), .Q(d_ff_7_q));  // open: Qn, preset, en, reset
  D_Flip_Flop #(.trigger("falling")) d_ff_8 (
    .clk(and_16_out), .D(Entrada[10]), .Q(d_ff_8_q));  // open: Qn, preset, en, reset
  and and_17 (and_17_out, d_ff_1_q, and_1_out);
  and and_18 (and_18_out, d_ff_2_q, and_3_out);
  and and_19 (and_19_out, d_ff_3_q, and_5_out);
  and and_20 (and_20_out, d_ff_4_q, and_7_out);
  and and_21 (and_21_out, d_ff_5_q, and_9_out);
  and and_22 (and_22_out, d_ff_6_q, and_11_out);
  and and_23 (and_23_out, d_ff_7_q, and_13_out);
  and and_24 (and_24_out, d_ff_8_q, and_15_out);
  or or_1 (or_11_out[10], and_24_out, and_23_out, and_22_out, and_21_out, and_20_out, and_19_out, and_18_out, and_17_out);
  D_Flip_Flop #(.trigger("falling")) d_ff_9 (
    .clk(and_2_out), .D(Entrada[9]), .Q(d_ff_9_q));  // open: Qn, preset, en, reset
  and and_25 (and_25_out, d_ff_9_q, and_1_out);
  D_Flip_Flop #(.trigger("falling")) d_ff_10 (
    .clk(and_4_out), .D(Entrada[9]), .Q(d_ff_10_q));  // open: Qn, preset, en, reset
  and and_26 (and_26_out, d_ff_10_q, and_3_out);
  D_Flip_Flop #(.trigger("falling")) d_ff_11 (
    .clk(and_6_out), .D(Entrada[9]), .Q(d_ff_11_q));  // open: Qn, preset, en, reset
  and and_27 (and_27_out, d_ff_11_q, and_5_out);
  D_Flip_Flop #(.trigger("falling")) d_ff_12 (
    .clk(and_8_out), .D(Entrada[9]), .Q(d_ff_12_q));  // open: Qn, preset, en, reset
  and and_28 (and_28_out, d_ff_12_q, and_7_out);
  D_Flip_Flop #(.trigger("falling")) d_ff_13 (
    .clk(and_10_out), .D(Entrada[9]), .Q(d_ff_13_q));  // open: Qn, preset, en, reset
  and and_29 (and_29_out, d_ff_13_q, and_9_out);
  D_Flip_Flop #(.trigger("falling")) d_ff_14 (
    .clk(and_12_out), .D(Entrada[9]), .Q(d_ff_14_q));  // open: Qn, preset, en, reset
  and and_30 (and_30_out, d_ff_14_q, and_11_out);
  D_Flip_Flop #(.trigger("falling")) d_ff_15 (
    .clk(and_14_out), .D(Entrada[9]), .Q(d_ff_15_q));  // open: Qn, preset, en, reset
  and and_31 (and_31_out, d_ff_15_q, and_13_out);
  D_Flip_Flop #(.trigger("falling")) d_ff_16 (
    .clk(and_16_out), .D(Entrada[9]), .Q(d_ff_16_q));  // open: Qn, preset, en, reset
  and and_32 (and_32_out, d_ff_16_q, and_15_out);
  or or_2 (or_11_out[9], and_32_out, and_31_out, and_30_out, and_29_out, and_28_out, and_27_out, and_26_out, and_25_out);
  D_Flip_Flop #(.trigger("falling")) d_ff_17 (
    .clk(and_2_out), .D(Entrada[8]), .Q(d_ff_17_q));  // open: Qn, preset, en, reset
  and and_33 (and_33_out, d_ff_17_q, and_1_out);
  D_Flip_Flop #(.trigger("falling")) d_ff_18 (
    .clk(and_4_out), .D(Entrada[8]), .Q(d_ff_18_q));  // open: Qn, preset, en, reset
  and and_34 (and_34_out, d_ff_18_q, and_3_out);
  D_Flip_Flop #(.trigger("falling")) d_ff_19 (
    .clk(and_6_out), .D(Entrada[8]), .Q(d_ff_19_q));  // open: Qn, preset, en, reset
  and and_35 (and_35_out, d_ff_19_q, and_5_out);
  D_Flip_Flop #(.trigger("falling")) d_ff_20 (
    .clk(and_8_out), .D(Entrada[8]), .Q(d_ff_20_q));  // open: Qn, preset, en, reset
  and and_36 (and_36_out, d_ff_20_q, and_7_out);
  D_Flip_Flop #(.trigger("falling")) d_ff_21 (
    .clk(and_10_out), .D(Entrada[8]), .Q(d_ff_21_q));  // open: Qn, preset, en, reset
  and and_37 (and_37_out, d_ff_21_q, and_9_out);
  D_Flip_Flop #(.trigger("falling")) d_ff_22 (
    .clk(and_12_out), .D(Entrada[8]), .Q(d_ff_22_q));  // open: Qn, preset, en, reset
  and and_38 (and_38_out, d_ff_22_q, and_11_out);
  D_Flip_Flop #(.trigger("falling")) d_ff_23 (
    .clk(and_14_out), .D(Entrada[8]), .Q(d_ff_23_q));  // open: Qn, preset, en, reset
  and and_39 (and_39_out, d_ff_23_q, and_13_out);
  D_Flip_Flop #(.trigger("falling")) d_ff_24 (
    .clk(and_16_out), .D(Entrada[8]), .Q(d_ff_24_q));  // open: Qn, preset, en, reset
  and and_40 (and_40_out, d_ff_24_q, and_15_out);
  or or_3 (or_11_out[8], and_40_out, and_39_out, and_38_out, and_37_out, and_36_out, and_35_out, and_34_out, and_33_out);
  D_Flip_Flop #(.trigger("falling")) d_ff_25 (
    .clk(and_2_out), .D(Entrada[7]), .Q(d_ff_25_q));  // open: Qn, preset, en, reset
  and and_41 (and_41_out, d_ff_25_q, and_1_out);
  D_Flip_Flop #(.trigger("falling")) d_ff_26 (
    .clk(and_4_out), .D(Entrada[7]), .Q(d_ff_26_q));  // open: Qn, preset, en, reset
  and and_42 (and_42_out, d_ff_26_q, and_3_out);
  D_Flip_Flop #(.trigger("falling")) d_ff_27 (
    .clk(and_6_out), .D(Entrada[7]), .Q(d_ff_27_q));  // open: Qn, preset, en, reset
  and and_43 (and_43_out, d_ff_27_q, and_5_out);
  D_Flip_Flop #(.trigger("falling")) d_ff_28 (
    .clk(and_8_out), .D(Entrada[7]), .Q(d_ff_28_q));  // open: Qn, preset, en, reset
  and and_44 (and_44_out, d_ff_28_q, and_7_out);
  D_Flip_Flop #(.trigger("falling")) d_ff_29 (
    .clk(and_10_out), .D(Entrada[7]), .Q(d_ff_29_q));  // open: Qn, preset, en, reset
  and and_45 (and_45_out, d_ff_29_q, and_9_out);
  D_Flip_Flop #(.trigger("falling")) d_ff_30 (
    .clk(and_12_out), .D(Entrada[7]), .Q(d_ff_30_q));  // open: Qn, preset, en, reset
  and and_46 (and_46_out, d_ff_30_q, and_11_out);
  D_Flip_Flop #(.trigger("falling")) d_ff_31 (
    .clk(and_14_out), .D(Entrada[7]), .Q(d_ff_31_q));  // open: Qn, preset, en, reset
  and and_47 (and_47_out, d_ff_31_q, and_13_out);
  D_Flip_Flop #(.trigger("falling")) d_ff_32 (
    .clk(and_16_out), .D(Entrada[7]), .Q(d_ff_32_q));  // open: Qn, preset, en, reset
  and and_48 (and_48_out, d_ff_32_q, and_15_out);
  or or_4 (or_11_out[7], and_48_out, and_47_out, and_46_out, and_45_out, and_44_out, and_43_out, and_42_out, and_41_out);
  D_Flip_Flop #(.trigger("falling")) d_ff_33 (
    .clk(and_2_out), .D(Entrada[6]), .Q(d_ff_33_q));  // open: Qn, preset, en, reset
  D_Flip_Flop #(.trigger("falling")) d_ff_34 (
    .clk(and_4_out), .D(Entrada[6]), .Q(d_ff_34_q));  // open: Qn, preset, en, reset
  D_Flip_Flop #(.trigger("falling")) d_ff_35 (
    .clk(and_6_out), .D(Entrada[6]), .Q(d_ff_35_q));  // open: Qn, preset, en, reset
  D_Flip_Flop #(.trigger("falling")) d_ff_36 (
    .clk(and_8_out), .D(Entrada[6]), .Q(d_ff_36_q));  // open: Qn, preset, en, reset
  D_Flip_Flop #(.trigger("falling")) d_ff_37 (
    .clk(and_10_out), .D(Entrada[6]), .Q(d_ff_37_q));  // open: Qn, preset, en, reset
  D_Flip_Flop #(.trigger("falling")) d_ff_38 (
    .clk(and_12_out), .D(Entrada[6]), .Q(d_ff_38_q));  // open: Qn, preset, en, reset
  D_Flip_Flop #(.trigger("falling")) d_ff_39 (
    .clk(and_14_out), .D(Entrada[6]), .Q(d_ff_39_q));  // open: Qn, preset, en, reset
  D_Flip_Flop #(.trigger("falling")) d_ff_40 (
    .clk(and_16_out), .D(Entrada[6]), .Q(d_ff_40_q));  // open: Qn, preset, en, reset
  and and_49 (and_49_out, d_ff_33_q, and_1_out);
  and and_50 (and_50_out, d_ff_34_q, and_3_out);
  and and_51 (and_51_out, d_ff_35_q, and_5_out);
  and and_52 (and_52_out, d_ff_36_q, and_7_out);
  and and_53 (and_53_out, d_ff_37_q, and_9_out);
  and and_54 (and_54_out, d_ff_38_q, and_11_out);
  and and_55 (and_55_out, d_ff_39_q, and_13_out);
  and and_56 (and_56_out, d_ff_40_q, and_15_out);
  or or_5 (or_11_out[6], and_56_out, and_55_out, and_54_out, and_53_out, and_52_out, and_51_out, and_50_out, and_49_out);
  D_Flip_Flop #(.trigger("falling")) d_ff_41 (
    .clk(and_2_out), .D(Entrada[5]), .Q(d_ff_41_q));  // open: Qn, preset, en, reset
  and and_57 (and_57_out, d_ff_41_q, and_1_out);
  D_Flip_Flop #(.trigger("falling")) d_ff_42 (
    .clk(and_4_out), .D(Entrada[5]), .Q(d_ff_42_q));  // open: Qn, preset, en, reset
  and and_58 (and_58_out, d_ff_42_q, and_3_out);
  D_Flip_Flop #(.trigger("falling")) d_ff_43 (
    .clk(and_6_out), .D(Entrada[5]), .Q(d_ff_43_q));  // open: Qn, preset, en, reset
  and and_59 (and_59_out, d_ff_43_q, and_5_out);
  D_Flip_Flop #(.trigger("falling")) d_ff_44 (
    .clk(and_8_out), .D(Entrada[5]), .Q(d_ff_44_q));  // open: Qn, preset, en, reset
  and and_60 (and_60_out, d_ff_44_q, and_7_out);
  D_Flip_Flop #(.trigger("falling")) d_ff_45 (
    .clk(and_10_out), .D(Entrada[5]), .Q(d_ff_45_q));  // open: Qn, preset, en, reset
  and and_61 (and_61_out, d_ff_45_q, and_9_out);
  D_Flip_Flop #(.trigger("falling")) d_ff_46 (
    .clk(and_12_out), .D(Entrada[5]), .Q(d_ff_46_q));  // open: Qn, preset, en, reset
  and and_62 (and_62_out, d_ff_46_q, and_11_out);
  D_Flip_Flop #(.trigger("falling")) d_ff_47 (
    .clk(and_14_out), .D(Entrada[5]), .Q(d_ff_47_q));  // open: Qn, preset, en, reset
  and and_63 (and_63_out, d_ff_47_q, and_13_out);
  D_Flip_Flop #(.trigger("falling")) d_ff_48 (
    .clk(and_16_out), .D(Entrada[5]), .Q(d_ff_48_q));  // open: Qn, preset, en, reset
  and and_64 (and_64_out, d_ff_48_q, and_15_out);
  or or_6 (or_11_out[5], and_64_out, and_63_out, and_62_out, and_61_out, and_60_out, and_59_out, and_58_out, and_57_out);
  D_Flip_Flop #(.trigger("falling")) d_ff_49 (
    .clk(and_2_out), .D(Entrada[4]), .Q(d_ff_49_q));  // open: Qn, preset, en, reset
  and and_65 (and_65_out, d_ff_49_q, and_1_out);
  D_Flip_Flop #(.trigger("falling")) d_ff_50 (
    .clk(and_4_out), .D(Entrada[4]), .Q(d_ff_50_q));  // open: Qn, preset, en, reset
  and and_66 (and_66_out, d_ff_50_q, and_3_out);
  D_Flip_Flop #(.trigger("falling")) d_ff_51 (
    .clk(and_6_out), .D(Entrada[4]), .Q(d_ff_51_q));  // open: Qn, preset, en, reset
  and and_67 (and_67_out, d_ff_51_q, and_5_out);
  D_Flip_Flop #(.trigger("falling")) d_ff_52 (
    .clk(and_8_out), .D(Entrada[4]), .Q(d_ff_52_q));  // open: Qn, preset, en, reset
  and and_68 (and_68_out, d_ff_52_q, and_7_out);
  D_Flip_Flop #(.trigger("falling")) d_ff_53 (
    .clk(and_10_out), .D(Entrada[4]), .Q(d_ff_53_q));  // open: Qn, preset, en, reset
  and and_69 (and_69_out, d_ff_53_q, and_9_out);
  D_Flip_Flop #(.trigger("falling")) d_ff_54 (
    .clk(and_12_out), .D(Entrada[4]), .Q(d_ff_54_q));  // open: Qn, preset, en, reset
  and and_70 (and_70_out, d_ff_54_q, and_11_out);
  D_Flip_Flop #(.trigger("falling")) d_ff_55 (
    .clk(and_14_out), .D(Entrada[4]), .Q(d_ff_55_q));  // open: Qn, preset, en, reset
  and and_71 (and_71_out, d_ff_55_q, and_13_out);
  D_Flip_Flop #(.trigger("falling")) d_ff_56 (
    .clk(and_16_out), .D(Entrada[4]), .Q(d_ff_56_q));  // open: Qn, preset, en, reset
  and and_72 (and_72_out, d_ff_56_q, and_15_out);
  or or_7 (or_11_out[4], and_72_out, and_71_out, and_70_out, and_69_out, and_68_out, and_67_out, and_66_out, and_65_out);
  D_Flip_Flop #(.trigger("falling")) d_ff_57 (
    .clk(and_2_out), .D(Entrada[3]), .Q(d_ff_57_q));  // open: Qn, preset, en, reset
  and and_73 (and_73_out, d_ff_57_q, and_1_out);
  D_Flip_Flop #(.trigger("falling")) d_ff_58 (
    .clk(and_4_out), .D(Entrada[3]), .Q(d_ff_58_q));  // open: Qn, preset, en, reset
  and and_74 (and_74_out, d_ff_58_q, and_3_out);
  D_Flip_Flop #(.trigger("falling")) d_ff_59 (
    .clk(and_6_out), .D(Entrada[3]), .Q(d_ff_59_q));  // open: Qn, preset, en, reset
  and and_75 (and_75_out, d_ff_59_q, and_5_out);
  D_Flip_Flop #(.trigger("falling")) d_ff_60 (
    .clk(and_8_out), .D(Entrada[3]), .Q(d_ff_60_q));  // open: Qn, preset, en, reset
  and and_76 (and_76_out, d_ff_60_q, and_7_out);
  D_Flip_Flop #(.trigger("falling")) d_ff_61 (
    .clk(and_10_out), .D(Entrada[3]), .Q(d_ff_61_q));  // open: Qn, preset, en, reset
  and and_77 (and_77_out, d_ff_61_q, and_9_out);
  D_Flip_Flop #(.trigger("falling")) d_ff_62 (
    .clk(and_12_out), .D(Entrada[3]), .Q(d_ff_62_q));  // open: Qn, preset, en, reset
  and and_78 (and_78_out, d_ff_62_q, and_11_out);
  D_Flip_Flop #(.trigger("falling")) d_ff_63 (
    .clk(and_14_out), .D(Entrada[3]), .Q(d_ff_63_q));  // open: Qn, preset, en, reset
  and and_79 (and_79_out, d_ff_63_q, and_13_out);
  D_Flip_Flop #(.trigger("falling")) d_ff_64 (
    .clk(and_16_out), .D(Entrada[3]), .Q(d_ff_64_q));  // open: Qn, preset, en, reset
  and and_80 (and_80_out, d_ff_64_q, and_15_out);
  or or_8 (or_11_out[3], and_80_out, and_79_out, and_78_out, and_77_out, and_76_out, and_75_out, and_74_out, and_73_out);
  D_Flip_Flop #(.trigger("falling")) d_ff_65 (
    .clk(and_2_out), .D(Entrada[2]), .Q(d_ff_65_q));  // open: Qn, preset, en, reset
  D_Flip_Flop #(.trigger("falling")) d_ff_66 (
    .clk(and_4_out), .D(Entrada[2]), .Q(d_ff_66_q));  // open: Qn, preset, en, reset
  D_Flip_Flop #(.trigger("falling")) d_ff_67 (
    .clk(and_6_out), .D(Entrada[2]), .Q(d_ff_67_q));  // open: Qn, preset, en, reset
  D_Flip_Flop #(.trigger("falling")) d_ff_68 (
    .clk(and_8_out), .D(Entrada[2]), .Q(d_ff_68_q));  // open: Qn, preset, en, reset
  D_Flip_Flop #(.trigger("falling")) d_ff_69 (
    .clk(and_10_out), .D(Entrada[2]), .Q(d_ff_69_q));  // open: Qn, preset, en, reset
  D_Flip_Flop #(.trigger("falling")) d_ff_70 (
    .clk(and_12_out), .D(Entrada[2]), .Q(d_ff_70_q));  // open: Qn, preset, en, reset
  D_Flip_Flop #(.trigger("falling")) d_ff_71 (
    .clk(and_14_out), .D(Entrada[2]), .Q(d_ff_71_q));  // open: Qn, preset, en, reset
  D_Flip_Flop #(.trigger("falling")) d_ff_72 (
    .clk(and_16_out), .D(Entrada[2]), .Q(d_ff_72_q));  // open: Qn, preset, en, reset
  and and_81 (and_81_out, d_ff_65_q, and_1_out);
  and and_82 (and_82_out, d_ff_66_q, and_3_out);
  and and_83 (and_83_out, d_ff_67_q, and_5_out);
  and and_84 (and_84_out, d_ff_68_q, and_7_out);
  and and_85 (and_85_out, d_ff_69_q, and_9_out);
  and and_86 (and_86_out, d_ff_70_q, and_11_out);
  and and_87 (and_87_out, d_ff_71_q, and_13_out);
  and and_88 (and_88_out, d_ff_72_q, and_15_out);
  or or_9 (or_11_out[2], and_88_out, and_87_out, and_86_out, and_85_out, and_84_out, and_83_out, and_82_out, and_81_out);
  D_Flip_Flop #(.trigger("falling")) d_ff_73 (
    .clk(and_2_out), .D(Entrada[1]), .Q(d_ff_73_q));  // open: Qn, preset, en, reset
  and and_89 (and_89_out, d_ff_73_q, and_1_out);
  D_Flip_Flop #(.trigger("falling")) d_ff_74 (
    .clk(and_4_out), .D(Entrada[1]), .Q(d_ff_74_q));  // open: Qn, preset, en, reset
  and and_90 (and_90_out, d_ff_74_q, and_3_out);
  D_Flip_Flop #(.trigger("falling")) d_ff_75 (
    .clk(and_6_out), .D(Entrada[1]), .Q(d_ff_75_q));  // open: Qn, preset, en, reset
  and and_91 (and_91_out, d_ff_75_q, and_5_out);
  D_Flip_Flop #(.trigger("falling")) d_ff_76 (
    .clk(and_8_out), .D(Entrada[1]), .Q(d_ff_76_q));  // open: Qn, preset, en, reset
  and and_92 (and_92_out, d_ff_76_q, and_7_out);
  D_Flip_Flop #(.trigger("falling")) d_ff_77 (
    .clk(and_10_out), .D(Entrada[1]), .Q(d_ff_77_q));  // open: Qn, preset, en, reset
  and and_93 (and_93_out, d_ff_77_q, and_9_out);
  D_Flip_Flop #(.trigger("falling")) d_ff_78 (
    .clk(and_12_out), .D(Entrada[1]), .Q(d_ff_78_q));  // open: Qn, preset, en, reset
  and and_94 (and_94_out, d_ff_78_q, and_11_out);
  D_Flip_Flop #(.trigger("falling")) d_ff_79 (
    .clk(and_14_out), .D(Entrada[1]), .Q(d_ff_79_q));  // open: Qn, preset, en, reset
  and and_95 (and_95_out, d_ff_79_q, and_13_out);
  D_Flip_Flop #(.trigger("falling")) d_ff_80 (
    .clk(and_16_out), .D(Entrada[1]), .Q(d_ff_80_q));  // open: Qn, preset, en, reset
  and and_96 (and_96_out, d_ff_80_q, and_15_out);
  or or_10 (or_11_out[1], and_96_out, and_95_out, and_94_out, and_93_out, and_92_out, and_91_out, and_90_out, and_89_out);
  D_Flip_Flop #(.trigger("falling")) d_ff_81 (
    .clk(and_2_out), .D(Entrada[0]), .Q(d_ff_81_q));  // open: Qn, preset, en, reset
  and and_97 (and_97_out, d_ff_81_q, and_1_out);
  D_Flip_Flop #(.trigger("falling")) d_ff_82 (
    .clk(and_4_out), .D(Entrada[0]), .Q(d_ff_82_q));  // open: Qn, preset, en, reset
  and and_98 (and_98_out, d_ff_82_q, and_3_out);
  D_Flip_Flop #(.trigger("falling")) d_ff_83 (
    .clk(and_6_out), .D(Entrada[0]), .Q(d_ff_83_q));  // open: Qn, preset, en, reset
  and and_99 (and_99_out, d_ff_83_q, and_5_out);
  D_Flip_Flop #(.trigger("falling")) d_ff_84 (
    .clk(and_8_out), .D(Entrada[0]), .Q(d_ff_84_q));  // open: Qn, preset, en, reset
  and and_100 (and_100_out, d_ff_84_q, and_7_out);
  D_Flip_Flop #(.trigger("falling")) d_ff_85 (
    .clk(and_10_out), .D(Entrada[0]), .Q(d_ff_85_q));  // open: Qn, preset, en, reset
  and and_101 (and_101_out, d_ff_85_q, and_9_out);
  D_Flip_Flop #(.trigger("falling")) d_ff_86 (
    .clk(and_12_out), .D(Entrada[0]), .Q(d_ff_86_q));  // open: Qn, preset, en, reset
  and and_102 (and_102_out, d_ff_86_q, and_11_out);
  D_Flip_Flop #(.trigger("falling")) d_ff_87 (
    .clk(and_14_out), .D(Entrada[0]), .Q(d_ff_87_q));  // open: Qn, preset, en, reset
  and and_103 (and_103_out, d_ff_87_q, and_13_out);
  D_Flip_Flop #(.trigger("falling")) d_ff_88 (
    .clk(and_16_out), .D(Entrada[0]), .Q(d_ff_88_q));  // open: Qn, preset, en, reset
  and and_104 (and_104_out, d_ff_88_q, and_15_out);
  or or_11 (or_11_out[0], and_104_out, and_103_out, and_102_out, and_101_out, and_100_out, and_99_out, and_98_out, and_97_out);
  ula ula_1 (.A(out_3), .B(or_11_out[7:0]), .in_3(or_11_out[10:8]), .out_4(ula_1_out_4));
  D_Flip_Flop d_ff_89 (.clk(clock_1_out), .D(ula_1_out_4[7]), .Q(out_3[7]));  // open: Qn, preset, en, reset
  D_Flip_Flop d_ff_90 (.clk(clock_1_out), .D(ula_1_out_4[6]), .Q(out_3[6]));  // open: Qn, preset, en, reset
  D_Flip_Flop d_ff_91 (.clk(clock_1_out), .D(ula_1_out_4[5]), .Q(out_3[5]));  // open: Qn, preset, en, reset
  D_Flip_Flop d_ff_92 (.clk(clock_1_out), .D(ula_1_out_4[4]), .Q(out_3[4]));  // open: Qn, preset, en, reset
  D_Flip_Flop d_ff_93 (.clk(clock_1_out), .D(ula_1_out_4[3]), .Q(out_3[3]));  // open: Qn, preset, en, reset
  D_Flip_Flop d_ff_94 (.clk(clock_1_out), .D(ula_1_out_4[2]), .Q(out_3[2]));  // open: Qn, preset, en, reset
  D_Flip_Flop d_ff_95 (.clk(clock_1_out), .D(ula_1_out_4[1]), .Q(out_3[1]));  // open: Qn, preset, en, reset
  D_Flip_Flop d_ff_96 (.clk(clock_1_out), .D(ula_1_out_4[0]), .Q(out_3[0]));  // open: Qn, preset, en, reset

  // Notes on the sheet:
  //   AND 000
  //   OR 001
  //   XOR 010
  //   SOMA 011
  //   SUBTRAÇÃO 100
  //   MULTIPLICAÇÃO 101
  //   DIVISÃO 110
  //   MOD 111
endmodule

module somador1bit (
  input  A,
  input  B,
  input  CIn,
  output S
);

  wire xor_1_out;

  xor xor_1 (xor_1_out, B, CIn);
  xor xor_2 (S, A, xor_1_out);
endmodule

module somador8bit (
  input  [7:0] A,
  input  [7:0] B,
  input  Operador,
  output [7:0] B_2
);

  wire and_1_out, and_2_out, and_3_out, and_4_out, and_5_out, and_6_out, and_7_out, and_8_out, and_9_out,
       and_10_out, and_11_out, and_12_out, and_13_out, and_14_out, and_15_out, and_16_out, and_17_out,
       and_18_out, and_19_out, and_20_out, and_21_out, and_22_out, and_23_out, and_24_out, and_25_out,
       and_26_out, and_27_out, and_28_out, G0_out, G1_out, G2_out, G3_out, G4_out, G5_out, G6_out, or_1_out,
       or_2_out, or_3_out, or_4_out, or_5_out, or_6_out, or_7_out, P0_out, P1_out, P2_out, P3_out, P4_out,
       P5_out, P6_out, xor_1_out, xor_2_out, xor_3_out, xor_4_out, xor_5_out, xor_6_out, xor_7_out, xor_8_out;

  xor xor_1 (xor_1_out, B[0], Operador);
  xor xor_2 (xor_2_out, B[1], Operador);
  xor xor_3 (xor_3_out, B[2], Operador);
  xor xor_4 (xor_4_out, B[3], Operador);
  xor xor_5 (xor_5_out, B[4], Operador);
  xor xor_6 (xor_6_out, B[5], Operador);
  xor xor_7 (xor_7_out, B[6], Operador);
  xor xor_8 (xor_8_out, B[7], Operador);
  somador1bit somador1bit_1 (.A(A[7]), .B(xor_8_out), .CIn(or_1_out), .S(B_2[7]));
  and and_1 (and_1_out, P6_out, P5_out, P4_out, P3_out, P2_out, P1_out, P0_out, Operador);
  and and_2 (and_2_out, P6_out, P5_out, P4_out, P3_out, P2_out, P1_out, G0_out);
  and and_3 (and_3_out, P6_out, P5_out, P4_out, P3_out, P2_out, G1_out);
  and and_4 (and_4_out, P6_out, P5_out, P4_out, P3_out, G2_out);
  and and_5 (and_5_out, P6_out, P5_out, P4_out, G3_out);
  or P6 (P6_out, A[6], xor_7_out);
  and and_6 (and_6_out, P6_out, P5_out, G4_out);
  and G6 (G6_out, A[6], xor_7_out);
  and and_7 (and_7_out, P6_out, G5_out);
  or or_1 (or_1_out, and_1_out, and_2_out, and_3_out, and_4_out, and_5_out, and_6_out, and_7_out, G6_out);
  and and_8 (and_8_out, Operador, P1_out, P2_out, P3_out, P4_out, P5_out, P0_out);
  somador1bit somador1bit_2 (.A(A[6]), .B(xor_7_out), .CIn(or_2_out), .S(B_2[6]));
  and and_9 (and_9_out, G0_out, P1_out, P2_out, P3_out, P4_out, P5_out);
  and and_10 (and_10_out, G1_out, P2_out, P3_out, P4_out, P5_out);
  and and_11 (and_11_out, P5_out, G2_out, P4_out, P3_out);
  or P5 (P5_out, A[5], xor_6_out);
  and and_12 (and_12_out, P5_out, G3_out, P4_out);
  and G5 (G5_out, A[5], xor_6_out);
  and and_13 (and_13_out, P5_out, G4_out);
  or or_2 (or_2_out, and_8_out, and_9_out, and_10_out, and_11_out, and_12_out, and_13_out, G5_out);
  somador1bit somador1bit_3 (.A(A[5]), .B(xor_6_out), .CIn(or_3_out), .S(B_2[5]));
  and and_14 (and_14_out, Operador, P0_out, P1_out, P2_out, P3_out, P4_out);
  and and_15 (and_15_out, P4_out, P2_out, P3_out, G1_out);
  and and_16 (and_16_out, P4_out, P3_out, P2_out, P1_out, G0_out);
  and and_17 (and_17_out, P4_out, P3_out, G2_out);
  or P4 (P4_out, A[4], xor_5_out);
  and and_18 (and_18_out, P4_out, G3_out);
  or or_3 (or_3_out, and_14_out, and_16_out, and_15_out, and_17_out, and_18_out, G4_out);
  and G4 (G4_out, A[4], xor_5_out);
  and and_19 (and_19_out, Operador, P0_out, P1_out, P3_out, P2_out);
  somador1bit somador1bit_4 (.A(A[4]), .B(xor_5_out), .CIn(or_4_out), .S(B_2[4]));
  and and_20 (and_20_out, P3_out, P0_out, P2_out, G0_out);
  and and_21 (and_21_out, P3_out, P2_out, G1_out);
  or P3 (P3_out, A[3], xor_4_out);
  and and_22 (and_22_out, P3_out, G2_out);
  and G3 (G3_out, A[3], xor_4_out);
  or or_4 (or_4_out, and_19_out, and_20_out, and_21_out, and_22_out, G3_out);
  and and_23 (and_23_out, Operador, P0_out, P1_out, P2_out);
  somador1bit somador1bit_5 (.A(A[3]), .B(xor_4_out), .CIn(or_5_out), .S(B_2[3]));
  and and_24 (and_24_out, P2_out, P1_out, G0_out);
  or P2 (P2_out, A[2], xor_3_out);
  and and_25 (and_25_out, P2_out, G1_out);
  or or_5 (or_5_out, and_23_out, and_24_out, and_25_out, G2_out);
  and G2 (G2_out, A[2], xor_3_out);
  somador1bit somador1bit_6 (.A(A[2]), .B(xor_3_out), .CIn(or_6_out), .S(B_2[2]));
  or P1 (P1_out, A[1], xor_2_out);
  and and_26 (and_26_out, Operador, P1_out, P0_out);
  and G1 (G1_out, A[1], xor_2_out);
  and and_27 (and_27_out, P1_out, G0_out);
  or or_6 (or_6_out, and_26_out, and_27_out, G1_out);
  or P0 (P0_out, A[0], xor_1_out);
  and and_28 (and_28_out, Operador, P0_out);
  somador1bit somador1bit_7 (.A(A[1]), .B(xor_2_out), .CIn(or_7_out), .S(B_2[1]));
  and G0 (G0_out, A[0], xor_1_out);
  or or_7 (or_7_out, and_28_out, G0_out);
  somador1bit somador1bit_8 (.A(A[0]), .B(xor_1_out), .CIn(Operador), .S(B_2[0]));
endmodule

module ula (
  input  [7:0] A,
  input  [7:0] B,
  input  [2:0] in_3,
  output [7:0] out_4
);

  wire [7:0] and_2_out, and_3_out, and_4_out, and_5_out, and_6_out, and_7_out, and_8_out, and_9_out,
       and_10_out, divider_1_out, divider_1_rem, multiplier_1_out, or_2_out, somador8bit_1_b_2, xor_2_out;
  wire [7:7] AND_out, DIV_out, MOD_out, MULT_out, OR_out, SOMA_out, SUB_out, XOR_out;

  and AND (AND_out[7], ~in_3[0], ~in_3[1], ~in_3[2]);  // AND_Gate
  and OR (OR_out[7], in_3[0], ~in_3[1], ~in_3[2]);  // AND_Gate
  and XOR (XOR_out[7], ~in_3[0], in_3[1], ~in_3[2]);  // AND_Gate
  and SOMA (SOMA_out[7], in_3[0], in_3[1], ~in_3[2]);  // AND_Gate
  and SUB (SUB_out[7], ~in_3[1], ~in_3[0], in_3[2]);  // AND_Gate
  and MULT (MULT_out[7], in_3[0], ~in_3[1], in_3[2]);  // AND_Gate
  and DIV (DIV_out[7], ~in_3[0], in_3[1], in_3[2]);  // AND_Gate
  and MOD (MOD_out[7], in_3[0], in_3[1], in_3[2]);
  somador8bit somador8bit_1 (.A(A), .B(B), .Operador(SUB_out[7]), .B_2(somador8bit_1_b_2));
  Multiplier multiplier_1 (.a(A), .b(B), .out(multiplier_1_out));  // open: cin, cout
  Divider divider_1 (.a(A), .b(B), .out(divider_1_out), .rem(divider_1_rem));  // open: upper
  assign and_2_out = A & B;  // AND_Gate and_2, 8 bits wide
  assign or_2_out = A | B;  // OR_Gate or_2, 8 bits wide
  assign xor_2_out = A ^ B;  // XOR_Gate xor_2, 8 bits wide
  assign and_3_out = and_2_out & {8{AND_out[7]}};  // AND_Gate and_3, 8 bits wide
  assign and_4_out = or_2_out & {8{OR_out[7]}};  // AND_Gate and_4, 8 bits wide
  assign and_5_out = xor_2_out & {8{XOR_out[7]}};  // AND_Gate and_5, 8 bits wide
  assign and_6_out = somador8bit_1_b_2 & {8{SOMA_out[7]}};  // AND_Gate and_6, 8 bits wide
  assign and_7_out = somador8bit_1_b_2 & {8{SUB_out[7]}};  // AND_Gate and_7, 8 bits wide
  assign and_8_out = multiplier_1_out & {8{MULT_out[7]}};  // AND_Gate and_8, 8 bits wide
  assign and_9_out = divider_1_out & {8{DIV_out[7]}};  // AND_Gate and_9, 8 bits wide
  assign and_10_out = divider_1_rem & {8{MOD_out[7]}};  // AND_Gate and_10, 8 bits wide
  assign out_4 = and_3_out | and_4_out | and_5_out | and_6_out | and_7_out | and_8_out | and_9_out | and_10_out;  // OR_Gate or_3, 8 bits wide
endmodule
