// Logisim project relogio.circ as structural Verilog: 2 circuits, main circuit main
module main (
);

  wire and_1_out, and_2_out, and_3_out, and_4_out, and_5_out, and_6_out, and_7_out, clock_1_out,
       n7segmentos_1_a, n7segmentos_1_b, n7segmentos_1_c, n7segmentos_1_d, n7segmentos_1_e, n7segmentos_1_f,
       n7segmentos_1_g, n7segmentos_2_a, n7segmentos_2_b, n7segmentos_2_c, n7segmentos_2_d, n7segmentos_2_e,
       n7segmentos_2_f, n7segmentos_2_g, n7segmentos_3_a, n7segmentos_3_b, n7segmentos_3_c, n7segmentos_3_d,
       n7segmentos_3_e, n7segmentos_3_f, n7segmentos_3_g, n7segmentos_4_a, n7segmentos_4_b, n7segmentos_4_c,
       n7segmentos_4_d, n7segmentos_4_e, n7segmentos_4_f, n7segmentos_4_g, n7segmentos_5_a, n7segmentos_5_b,
       n7segmentos_5_c, n7segmentos_5_d, n7segmentos_5_e, n7segmentos_5_f, n7segmentos_5_g, n7segmentos_6_a,
       n7segmentos_6_b, n7segmentos_6_c, n7segmentos_6_d, n7segmentos_6_e, n7segmentos_6_f, n7segmentos_6_g,
       or_1_out, or_2_out;
  wire [3:0] H1, H2, M1, M2, S1, S2;

  or or_1 (or_1_out, or_2_out, H1[3]);
  T_Flip_Flop #(.trigger("falling")) t_ff_1 (
    .clk(and_5_out), .T(1'b1), .Q(H1[0]), .reset(or_2_out));  // open: Qn, preset, en
  or or_2 (or_2_out, and_1_out, and_2_out);
  T_Flip_Flop #(.trigger("falling")) t_ff_2 (
    .clk(or_1_out), .T(1'b1), .Q(H2[0]), .reset(and_3_out));  // open: Qn, preset, en
  T_Flip_Flop #(.trigger("falling")) t_ff_3 (
    .clk(H1[0]), .T(1'b1), .Q(H1[1]), .reset(or_2_out));  // open: Qn, preset, en
  and and_1 (and_1_out, H1[3], ~H1[2], H1[1], ~H1[0]);  // AND_Gate
  and and_2 (and_2_out, ~H1[0], ~H1[1], H1[2], ~H1[3], H2[1]);  // AND_Gate
  T_Flip_Flop #(.trigger("falling")) t_ff_4 (
    .clk(H2[0]), .T(1'b1), .Q(H2[1]), .reset(and_3_out));  // open: Qn, preset, en
  and and_3 (and_3_out, ~H2[3], ~H2[2], H2[1], H2[0]);  // AND_Gate
  T_Flip_Flop #(.trigger("falling")) t_ff_5 (
    .clk(H1[1]), .T(1'b1), .Q(H1[2]), .reset(or_2_out));  // open: Qn, preset, en
  T_Flip_Flop #(.trigger("falling")) t_ff_6 (
    .clk(H2[1]), .T(1'b1), .Q(H2[2]), .reset(and_3_out));  // open: Qn, preset, en
  T_Flip_Flop #(.trigger("falling")) t_ff_7 (
    .clk(H1[2]), .T(1'b1), .Q(H1[3]), .reset(or_2_out));  // open: Qn, preset, en
  T_Flip_Flop #(.trigger("falling")) t_ff_8 (
    .clk(H2[2]), .T(1'b1), .Q(H2[3]), .reset(and_3_out));  // open: Qn, preset, en
  _7_Segment_Display u_7_segment_display_1 (
    .g(n7segmentos_2_g), .f(n7segmentos_2_f), .a(n7segmentos_2_a), .b(n7segmentos_2_b), .e(n7segmentos_2_e),
    .d(n7segmentos_2_d), .c(n7segmentos_2_c));  // open: dp
  _7_Segment_Display u_7_segment_display_2 (
    .g(n7segmentos_1_g), .f(n7segmentos_1_f), .a(n7segmentos_1_a), .b(n7segmentos_1_b), .e(n7segmentos_1_e),
    .d(n7segmentos_1_d), .c(n7segmentos_1_c));  // open: dp
  _7segmentos u_7segmentos_1 (
    .in_1(H1), .a(n7segmentos_1_a), .b(n7segmentos_1_b), .c(n7segmentos_1_c), .d(n7segmentos_1_d),
    .e(n7segmentos_1_e), .f(n7segmentos_1_f), .g(n7segmentos_1_g));
  _7segmentos u_7segmentos_2 (
    .in_1(H2), .a(n7segmentos_2_a), .b(n7segmentos_2_b), .c(n7segmentos_2_c), .d(n7segmentos_2_d),
    .e(n7segmentos_2_e), .f(n7segmentos_2_f), .g(n7segmentos_2_g));
  T_Flip_Flop #(.trigger("falling")) t_ff_9 (
    .clk(and_7_out), .T(1'b1), .Q(M1[0]), .reset(and_4_out));  // open: Qn, preset, en
  T_Flip_Flop #(.trigger("falling")) t_ff_10 (
    .clk(M1[3]), .T(1'b1), .Q(M2[0]), .reset(and_5_out));  // open: Qn, preset, en
  _7_Segment_Display u_7_segment_display_3 (
    .g(n7segmentos_3_g), .f(n7segmentos_3_f), .a(n7segmentos_3_a), .b(n7segmentos_3_b), .e(n7segmentos_3_e),
    .d(n7segmentos_3_d), .c(n7segmentos_3_c));  // open: dp
  T_Flip_Flop #(.trigger("falling")) t_ff_11 (
    .clk(M1[0]), .T(1'b1), .Q(M1[1]), .reset(and_4_out));  // open: Qn, preset, en
  and and_4 (and_4_out, M1[3], ~M1[2], M1[1], ~M1[0]);  // AND_Gate
  and and_5 (and_5_out, ~M2[3], M2[2], M2[1], ~M2[0]);  // AND_Gate
  _7_Segment_Display u_7_segment_display_4 (
    .g(n7segmentos_4_g), .f(n7segmentos_4_f), .a(n7segmentos_4_a), .b(n7segmentos_4_b), .e(n7segmentos_4_e),
    .d(n7segmentos_4_d), .c(n7segmentos_4_c));  // open: dp
  _7segmentos u_7segmentos_3 (
    .in_1(M2), .a(n7segmentos_3_a), .b(n7segmentos_3_b), .c(n7segmentos_3_c), .d(n7segmentos_3_d),
    .e(n7segmentos_3_e), .f(n7segmentos_3_f), .g(n7segmentos_3_g));
  _7segmentos u_7segmentos_4 (
    .in_1(M1), .a(n7segmentos_4_a), .b(n7segmentos_4_b), .c(n7segmentos_4_c), .d(n7segmentos_4_d),
    .e(n7segmentos_4_e), .f(n7segmentos_4_f), .g(n7segmentos_4_g));
  T_Flip_Flop #(.trigger("falling")) t_ff_12 (
    .clk(M2[0]), .T(1'b1), .Q(M2[1]), .reset(and_5_out));  // open: Qn, preset, en
  _7_Segment_Display u_7_segment_display_5 (
    .g(n7segmentos_5_g), .f(n7segmentos_5_f), .a(n7segmentos_5_a), .b(n7segmentos_5_b), .e(n7segmentos_5_e),
    .d(n7segmentos_5_d), .c(n7segmentos_5_c));  // open: dp
  T_Flip_Flop #(.trigger("falling")) t_ff_13 (
    .clk(M1[1]), .T(1'b1), .Q(M1[2]), .reset(and_4_out));  // open: Qn, preset, en
  T_Flip_Flop #(.trigger("falling")) t_ff_14 (
    .clk(M2[1]), .T(1'b1), .Q(M2[2]), .reset(and_5_out));  // open: Qn, preset, en
  _7_Segment_Display u_7_segment_display_6 (
    .g(n7segmentos_6_g), .f(n7segmentos_6_f), .a(n7segmentos_6_a), .b(n7segmentos_6_b), .e(n7segmentos_6_e),
    .d(n7segmentos_6_d), .c(n7segmentos_6_c));  // open: dp
  _7segmentos u_7segmentos_5 (
    .in_1(S2), .a(n7segmentos_5_a), .b(n7segmentos_5_b), .c(n7segmentos_5_c), .d(n7segmentos_5_d),
    .e(n7segmentos_5_e), .f(n7segmentos_5_f), .g(n7segmentos_5_g));
  _7segmentos u_7segmentos_6 (
    .in_1(S1), .a(n7segmentos_6_a), .b(n7segmentos_6_b), .c(n7segmentos_6_c), .d(n7segmentos_6_d),
    .e(n7segmentos_6_e), .f(n7segmentos_6_f), .g(n7segmentos_6_g));
  T_Flip_Flop #(.trigger("falling")) t_ff_15 (
    .clk(M1[2]), .T(1'b1), .Q(M1[3]), .reset(and_4_out));  // open: Qn, preset, en
  T_Flip_Flop #(.trigger("falling")) t_ff_16 (
    .clk(M2[2]), .T(1'b1), .Q(M2[3]), .reset(and_5_out));  // open: Qn, preset, en
  Clock clock_1 (.out(clock_1_out));
  T_Flip_Flop #(.trigger("falling")) t_ff_17 (
    .clk(clock_1_out), .T(1'b1), .Q(S1[0]), .reset(and_6_out));  // open: Qn, preset, en
  T_Flip_Flop #(.trigger("falling")) t_ff_18 (
    .clk(S1[3]), .T(1'b1), .Q(S2[0]), .reset(and_7_out));  // open: Qn, preset, en
  T_Flip_Flop #(.trigger("falling")) t_ff_19 (
    .clk(S1[0]), .T(1'b1), .Q(S1[1]), .reset(and_6_out));  // open: Qn, preset, en
  and and_6 (and_6_out, S1[3], ~S1[2], S1[1], ~S1[0]);  // AND_Gate
  T_Flip_Flop #(.trigger("falling")) t_ff_20 (
    .clk(S2[0]), .T(1'b1), .Q(S2[1]), .reset(and_7_out));  // open: Qn, preset, en
  and and_7 (and_7_out, ~S2[3], S2[2], S2[1], ~S2[0]);  // AND_Gate
  T_Flip_Flop #(.trigger("falling")) t_ff_21 (
    .clk(S1[1]), .T(1'b1), .Q(S1[2]), .reset(and_6_out));  // open: Qn, preset, en
  T_Flip_Flop #(.trigger("falling")) t_ff_22 (
    .clk(S2[1]), .T(1'b1), .Q(S2[2]), .reset(and_7_out));  // open: Qn, preset, en
  T_Flip_Flop #(.trigger("falling")) t_ff_23 (
    .clk(S1[2]), .T(1'b1), .Q(S1[3]), .reset(and_6_out));  // open: Qn, preset, en
  T_Flip_Flop #(.trigger("falling")) t_ff_24 (
    .clk(S2[2]), .T(1'b1), .Q(S2[3]), .reset(and_7_out));  // open: Qn, preset, en
endmodule

module _7segmentos (
  input  [3:0] in_1,
  output a,
  output b,
  output c,
  output d,
  output e,
  output f,
  output g
);

  wire and_1_out, and_2_out, and_3_out, and_4_out, and_5_out, and_6_out, and_7_out, and_8_out, and_9_out,
       and_10_out, and_11_out, and_12_out, and_13_out, and_14_out, and_15_out, and_16_out, not_1_out,
       not_2_out, not_3_out, not_4_out, not_5_out, not_6_out, not_7_out, not_8_out, not_9_out, not_10_out,
       not_11_out, not_12_out, not_13_out, not_14_out, not_15_out, not_16_out, not_17_out, not_18_out,
       not_19_out, not_20_out, not_21_out;

  not not_1 (not_1_out, in_1[2]);
  not not_2 (not_2_out, in_1[0]);
  not not_3 (not_3_out, in_1[1]);
  not not_4 (not_4_out, in_1[0]);
  not not_5 (not_5_out, in_1[1]);
  not not_6 (not_6_out, in_1[2]);
  not not_7 (not_7_out, in_1[0]);
  not not_8 (not_8_out, in_1[2]);
  not not_9 (not_9_out, in_1[0]);
  not not_10 (not_10_out, in_1[1]);
  not not_11 (not_11_out, in_1[2]);
  not not_12 (not_12_out, in_1[0]);
  not not_13 (not_13_out, in_1[0]);
  not not_14 (not_14_out, in_1[1]);
  not not_15 (not_15_out, in_1[0]);
  not not_16 (not_16_out, in_1[1]);
  not not_17 (not_17_out, in_1[0]);
  not not_18 (not_18_out, in_1[2]);
  not not_19 (not_19_out, in_1[1]);
  not not_20 (not_20_out, in_1[0]);
  and and_1 (and_1_out, not_1_out, not_2_out);
  and and_2 (and_2_out, in_1[2], in_1[0]);
  not not_21 (not_21_out, in_1[2]);
  and and_3 (and_3_out, not_3_out, not_4_out);
  and and_4 (and_4_out, in_1[1], in_1[0]);
  or or_1 (c, not_5_out, in_1[0], in_1[2]);
  and and_5 (and_5_out, not_6_out, not_7_out);
  and and_6 (and_6_out, not_8_out, in_1[1]);
  and and_7 (and_7_out, in_1[1], not_9_out);
  and and_8 (and_8_out, in_1[2], not_10_out, in_1[0]);
  and and_9 (and_9_out, not_11_out, not_12_out);
  and and_10 (and_10_out, in_1[1], not_13_out);
  and and_11 (and_11_out, not_14_out, not_15_out);
  and and_12 (and_12_out, in_1[2], not_16_out);
  and and_13 (and_13_out, in_1[2], not_17_out);
  and and_14 (and_14_out, not_18_out, in_1[1]);
  and and_15 (and_15_out, in_1[2], not_19_out);
  and and_16 (and_16_out, in_1[2], not_20_out);
  or or_2 (a, and_1_out, in_1[1], and_2_out, in_1[3]);
  or or_3 (b, not_21_out, and_3_out, and_4_out);
  or or_4 (d, and_5_out, and_6_out, and_7_out, and_8_out);
  or or_5 (e, and_9_out, and_10_out);
  or or_6 (f, and_11_out, and_12_out, and_13_out, in_1[3]);
  or or_7 (g, and_14_out, and_15_out, and_16_out, in_1[3]);
endmodule
