// Logisim project somador8bits.circ as structural Verilog
module somador (
  input  A,
  input  B,
  input  C,
  output S,
  output Cout
);

  wire and_1_out, and_2_out, and_3_out, xor_1_out;

  and and_1 (and_1_out, A, B);
  and and_2 (and_2_out, B, C);
  and and_3 (and_3_out, A, C);
  xor xor_1 (xor_1_out, B, C);
  or or_1 (Cout, and_1_out, and_2_out, and_3_out);
  xor xor_2 (S, A, xor_1_out);
endmodule

module somador8bit (
  input  in_1,
  input  in_2,
  input  in_3,
  input  in_4,
  input  in_5,
  input  in_6,
  input  in_7,
  input  in_8,
  input  in_9,
  input  in_10,
  input  in_11,
  input  in_12,
  input  in_13,
  input  in_14,
  input  in_15,
  input  in_16,
  output out_17,
  output out_18,
  output out_19,
  output out_20,
  output out_21,
  output out_22,
  output out_23,
  output out_24
);

  wire somador_1_p1, somador_1_p6, somador_3_cout, somador_4_cout, somador_5_cout, somador_6_cout,
       somador_7_cout, somador_8_cout;

  // somador somador_1: pin names not known; wires that end beside it: somador_1_p1, in_1, somador_1_p1, in_9, out_17, somador_1_p6
  somador somador_2 (.A(in_2), .B(in_10), .C(somador_3_cout), .S(out_18), .Cout(somador_1_p6));
  somador somador_3 (.A(in_3), .B(in_11), .C(somador_4_cout), .S(out_19), .Cout(somador_3_cout));
  somador somador_4 (.A(in_4), .B(in_12), .C(somador_5_cout), .S(out_20), .Cout(somador_4_cout));
  somador somador_5 (.A(in_5), .B(in_13), .C(somador_6_cout), .S(out_21), .Cout(somador_5_cout));
  somador somador_6 (.A(in_6), .B(in_14), .C(somador_8_cout), .S(out_22), .Cout(somador_6_cout));
  somador somador_7 (.A(in_8), .B(in_16), .C(1'b0), .S(out_24), .Cout(somador_7_cout));
  somador somador_8 (.A(in_7), .B(in_15), .C(somador_7_cout), .S(out_23), .Cout(somador_8_cout));
endmodule
