// Logisim project somadorLookahead + ula.circ as structural Verilog: 3 circuits, main circuit main
module main (
  input  [7:0] A,
  input  [7:0] B,
  input  [2:0] in_3,
  output [7:0] out_4
);

  wire [7:0] and_2_out, and_3_out, and_4_out, and_5_out, and_6_out, and_7_out, and_8_out, and_9_out,
       and_10_out, divider_1_out, divider_1_rem, multiplier_1_out, or_2_out, somador8bit_1_b_2, xor_2_out;
  wire [7:7] AND_out, DIV_out, MOD_out, MULT_out, OR_out, SOMA_out, SUB_out, XOR_out;

  and AND (AND_out[7], ~in_3[0], ~in_3[1], ~in_3[2]);  // AND_Gate
  and OR (OR_out[7], in_3[0], ~in_3[1], ~in_3[2]);  // AND_Gate
  and XOR (XOR_out[7], ~in_3[0], in_3[1], ~in_3[2]);  // AND_Gate
  and SOMA (SOMA_out[7], in_3[0], in_3[1], ~in_3[2]);  // AND_Gate
  and SUB (SUB_out[7], ~in_3[1], ~in_3[0], in_3[2]);  // AND_Gate
  and MULT (MULT_out[7], in_3[0], ~in_3[1], in_3[2]);  // AND_Gate
  and DIV (DIV_out[7], ~in_3[0], in_3[1], in_3[2]);  // AND_Gate
  and MOD (MOD_out[7], in_3[0], in_3[1], in_3[2]);
  somador8bit somador8bit_1 (.A(A), .B(B), .Operador(SUB_out[7]), .B_2(somador8bit_1_b_2));
  Multiplier multiplier_1 (.a(A), .b(B), .out(multiplier_1_out));  // open: cin, cout
  Divider divider_1 (.a(A), .b(B), .out(divider_1_out), .rem(divider_1_rem));  // open: upper
  assign and_2_out = A & B;  // AND_Gate and_2, 8 bits wide
  assign or_2_out = A | B;  // OR_Gate or_2, 8 bits wide
  assign xor_2_out = A ^ B;  // XOR_Gate xor_2, 8 bits wide
  assign and_3_out = and_2_out & {8{AND_out[7]}};  // AND_Gate and_3, 8 bits wide
  assign and_4_out = or_2_out & {8{OR_out[7]}};  // AND_Gate and_4, 8 bits wide
  assign and_5_out = xor_2_out & {8{XOR_out[7]}};  // AND_Gate and_5, 8 bits wide
  assign and_6_out = somador8bit_1_b_2 & {8{SOMA_out[7]}};  // AND_Gate and_6, 8 bits wide
  assign and_7_out = somador8bit_1_b_2 & {8{SUB_out[7]}};  // AND_Gate and_7, 8 bits wide
  assign and_8_out = multiplier_1_out & {8{MULT_out[7]}};  // AND_Gate and_8, 8 bits wide
  assign and_9_out = divider_1_out & {8{DIV_out[7]}};  // AND_Gate and_9, 8 bits wide
  assign and_10_out = divider_1_rem & {8{MOD_out[7]}};  // AND_Gate and_10, 8 bits wide
  assign out_4 = and_3_out | and_4_out | and_5_out | and_6_out | and_7_out | and_8_out | and_9_out | and_10_out;  // OR_Gate or_3, 8 bits wide
endmodule

module somador1bit (
  input  A,
  input  B,
  input  CIn,
  output S
);

  wire xor_1_out;

  xor xor_1 (xor_1_out, B, CIn);
  xor xor_2 (S, A, xor_1_out);
endmodule

module somador8bit (
  input  [7:0] A,
  input  [7:0] B,
  input  Operador,
  output [7:0] B_2
);

  wire and_1_out, and_2_out, and_3_out, and_4_out, and_5_out, and_6_out, and_7_out, and_8_out, and_9_out,
       and_10_out, and_11_out, and_12_out, and_13_out, and_14_out, and_15_out, and_16_out, and_17_out,
       and_18_out, and_19_out, and_20_out, and_21_out, and_22_out, and_23_out, and_24_out, and_25_out,
       and_26_out, and_27_out, and_28_out, G0_out, G1_out, G2_out, G3_out, G4_out, G5_out, G6_out, or_1_out,
       or_2_out, or_3_out, or_4_out, or_5_out, or_6_out, or_7_out, P0_out, P1_out, P2_out, P3_out, P4_out,
       P5_out, P6_out, xor_1_out, xor_2_out, xor_3_out, xor_4_out, xor_5_out, xor_6_out, xor_7_out, xor_8_out;

  xor xor_1 (xor_1_out, B[0], Operador);
  xor xor_2 (xor_2_out, B[1], Operador);
  xor xor_3 (xor_3_out, B[2], Operador);
  xor xor_4 (xor_4_out, B[3], Operador);
  xor xor_5 (xor_5_out, B[4], Operador);
  xor xor_6 (xor_6_out, B[5], Operador);
  xor xor_7 (xor_7_out, B[6], Operador);
  xor xor_8 (xor_8_out, B[7], Operador);
  somador1bit somador1bit_1 (.A(A[7]), .B(xor_8_out), .CIn(or_1_out), .S(B_2[7]));
  and and_1 (and_1_out, P6_out, P5_out, P4_out, P3_out, P2_out, P1_out, P0_out, Operador);
  and and_2 (and_2_out, P6_out, P5_out, P4_out, P3_out, P2_out, P1_out, G0_out);
  and and_3 (and_3_out, P6_out, P5_out, P4_out, P3_out, P2_out, G1_out);
  and and_4 (and_4_out, P6_out, P5_out, P4_out, P3_out, G2_out);
  and and_5 (and_5_out, P6_out, P5_out, P4_out, G3_out);
  or P6 (P6_out, A[6], xor_7_out);
  and and_6 (and_6_out, P6_out, P5_out, G4_out);
  and G6 (G6_out, A[6], xor_7_out);
  and and_7 (and_7_out, P6_out, G5_out);
  or or_1 (or_1_out, and_1_out, and_2_out, and_3_out, and_4_out, and_5_out, and_6_out, and_7_out, G6_out);
  and and_8 (and_8_out, Operador, P1_out, P2_out, P3_out, P4_out, P5_out, P0_out);
  somador1bit somador1bit_2 (.A(A[6]), .B(xor_7_out), .CIn(or_2_out), .S(B_2[6]));
  and and_9 (and_9_out, G0_out, P1_out, P2_out, P3_out, P4_out, P5_out);
  and and_10 (and_10_out, G1_out, P2_out, P3_out, P4_out, P5_out);
  and and_11 (and_11_out, P5_out, G2_out, P4_out, P3_out);
  or P5 (P5_out, A[5], xor_6_out);
  and and_12 (and_12_out, P5_out, G3_out, P4_out);
  and G5 (G5_out, A[5], xor_6_out);
  and and_13 (and_13_out, P5_out, G4_out);
  or or_2 (or_2_out, and_8_out, and_9_out, and_10_out, and_11_out, and_12_out, and_13_out, G5_out);
  somador1bit somador1bit_3 (.A(A[5]), .B(xor_6_out), .CIn(or_3_out), .S(B_2[5]));
  and and_14 (and_14_out, Operador, P0_out, P1_out, P2_out, P3_out, P4_out);
  and and_15 (and_15_out, P4_out, P2_out, P3_out, G1_out);
  and and_16 (and_16_out, P4_out, P3_out, P2_out, P1_out, G0_out);
  and and_17 (and_17_out, P4_out, P3_out, G2_out);
  or P4 (P4_out, A[4], xor_5_out);
  and and_18 (and_18_out, P4_out, G3_out);
  or or_3 (or_3_out, and_14_out, and_16_out, and_15_out, and_17_out, and_18_out, G4_out);
  and G4 (G4_out, A[4], xor_5_out);
  and and_19 (and_19_out, Operador, P0_out, P1_out, P3_out, P2_out);
  somador1bit somador1bit_4 (.A(A[4]), .B(xor_5_out), .CIn(or_4_out), .S(B_2[4]));
  and and_20 (and_20_out, P3_out, P0_out, P2_out, G0_out);
  and and_21 (and_21_out, P3_out, P2_out, G1_out);
  or P3 (P3_out, A[3], xor_4_out);
  and and_22 (and_22_out, P3_out, G2_out);
  and G3 (G3_out, A[3], xor_4_out);
  or or_4 (or_4_out, and_19_out, and_20_out, and_21_out, and_22_out, G3_out);
  and and_23 (and_23_out, Operador, P0_out, P1_out, P2_out);
  somador1bit somador1bit_5 (.A(A[3]), .B(xor_4_out), .CIn(or_5_out), .S(B_2[3]));
  and and_24 (and_24_out, P2_out, P1_out, G0_out);
  or P2 (P2_out, A[2], xor_3_out);
  and and_25 (and_25_out, P2_out, G1_out);
  or or_5 (or_5_out, and_23_out, and_24_out, and_25_out, G2_out);
  and G2 (G2_out, A[2], xor_3_out);
  somador1bit somador1bit_6 (.A(A[2]), .B(xor_3_out), .CIn(or_6_out), .S(B_2[2]));
  or P1 (P1_out, A[1], xor_2_out);
  and and_26 (and_26_out, Operador, P1_out, P0_out);
  and G1 (G1_out, A[1], xor_2_out);
  and and_27 (and_27_out, P1_out, G0_out);
  or or_6 (or_6_out, and_26_out, and_27_out, G1_out);
  or P0 (P0_out, A[0], xor_1_out);
  and and_28 (and_28_out, Operador, P0_out);
  somador1bit somador1bit_7 (.A(A[1]), .B(xor_2_out), .CIn(or_7_out), .S(B_2[1]));
  and G0 (G0_out, A[0], xor_1_out);
  or or_7 (or_7_out, and_28_out, G0_out);
  somador1bit somador1bit_8 (.A(A[0]), .B(xor_1_out), .CIn(Operador), .S(B_2[0]));
endmodule
