// Logisim project subtrator8bits.circ as structural Verilog
module subtrator1bit (
  input  A,
  input  B,
  input  COut,
  output S,
  output Cin
);

  wire and_1_out, and_2_out, and_3_out, not_1_out, not_2_out, xor_1_out;

  not not_1 (not_1_out, A);
  not not_2 (not_2_out, A);
  xor xor_1 (xor_1_out, B, COut);
  and and_1 (and_1_out, not_1_out, B);
  and and_2 (and_2_out, B, COut);
  and and_3 (and_3_out, not_2_out, COut);
  or or_1 (Cin, and_1_out, and_2_out, and_3_out);
  xor xor_2 (S, A, xor_1_out);
endmodule

module subtrator8bits (
  input  A,
  input  A_2,
  input  A_3,
  input  A_4,
  input  A_5,
  input  A_6,
  input  A_7,
  input  A_8,
  input  B,
  input  B_2,
  input  B_3,
  input  B_4,
  input  B_5,
  input  B_6,
  input  B_7,
  input  B_8,
  output out_17,
  output out_18,
  output out_19,
  output out_20,
  output out_21,
  output out_22,
  output out_23,
  output out_24
);

  wire subtrator1bit_1_cin, subtrator1bit_2_cin, subtrator1bit_3_cin, subtrator1bit_4_cin,
       subtrator1bit_5_cin, subtrator1bit_6_cin, subtrator1bit_7_cin, subtrator1bit_8_cin;

  subtrator1bit subtrator1bit_1 (.S(out_17), .Cin(subtrator1bit_1_cin), .A(A), .B(B), .COut(subtrator1bit_2_cin));
  subtrator1bit subtrator1bit_2 (.S(out_18), .Cin(subtrator1bit_2_cin), .A(A_2), .B(B_2), .COut(subtrator1bit_3_cin));
  subtrator1bit subtrator1bit_3 (.S(out_19), .Cin(subtrator1bit_3_cin), .A(A_3), .B(B_3), .COut(subtrator1bit_4_cin));
  subtrator1bit subtrator1bit_4 (.S(out_20), .Cin(subtrator1bit_4_cin), .A(A_4), .B(B_4), .COut(subtrator1bit_5_cin));
  subtrator1bit subtrator1bit_5 (.S(out_21), .Cin(subtrator1bit_5_cin), .A(A_5), .B(B_5), .COut(subtrator1bit_6_cin));
  subtrator1bit subtrator1bit_6 (.S(out_22), .Cin(subtrator1bit_6_cin), .A(A_6), .B(B_6), .COut(subtrator1bit_7_cin));
  subtrator1bit subtrator1bit_7 (.S(out_23), .Cin(subtrator1bit_7_cin), .A(A_7), .B(B_7), .COut(subtrator1bit_8_cin));
  subtrator1bit subtrator1bit_8 (.S(out_24), .Cin(subtrator1bit_8_cin), .A(A_8), .B(B_8), .COut(1'b0));
endmodule
